// Digital circuit hbaris_inlab1.dig as structural Verilog
module hbaris_inlab1 (
);

  wire _7486_1_pin3, _7486_1_pin5, _7486_1_pin6, _7486_1_pin8, switchdt_1_p1, switchdt_2_p1, switchdt_3_p1;

  // SwitchDT switchdt_1: pin names not known; wires that end beside it: switchdt_1_p1, 1'b1, 1'b0
  // SwitchDT switchdt_2: pin names not known; wires that end beside it: switchdt_2_p1, 1'b1, 1'b0
  // SwitchDT switchdt_3: pin names not known; wires that end beside it: switchdt_3_p1, 1'b1, 1'b0
  _7486 _7486_1 (
    .pin1(switchdt_1_p1), .pin2(switchdt_2_p1), .pin3(_7486_1_pin3), .pin4(switchdt_3_p1),
    .pin5(_7486_1_pin5), .pin6(_7486_1_pin6), .pin7(1'b0), .pin8(_7486_1_pin8), .pin9(_7486_1_pin6),
    .pin10(_7486_1_pin3), .pin12(1'b0), .pin13(1'b0), .pin14(1'b1));  // open: pin11
  // SwitchDT switchdt_4: pin names not known; wires that end beside it: _7486_1_pin5, 1'b1, 1'b0, 1'b0
  LED led_1 (.in(_7486_1_pin8));
  PowerSupply _5V (.VDD(1'b1), .GND(1'b0));
endmodule
