// Digital circuit mul_by_n.dig as structural Verilog
module mul_by_n (
  input  [3:0] in,
  output [7:0] out
);

  Add #(.Bits(8)) add_1 (.a({2'b00, in, 2'b00}), .b({4'b0000, in}), .c_i(1'b0), .s(out));  // open: c_o
endmodule
