// Digital circuit multiplier.dig as structural Verilog
module multiplier (
  input  in_1,
  input  in_2,
  input  in_3,
  input  in_4
);

  wire [3:0] binary2bcd_1_p2, binary2bcd_1_p3, binary2bcd_1_p4, unsignedbcd_1_p1, unsignedbcd_1_p3;
  wire [7:0] mul_by_n_1_out;

  Seven_Seg_Hex seven_seg_hex_1 (.d(unsignedbcd_1_p1), .dp(1'b0));
  Seven_Seg_Hex seven_seg_hex_2 (.d(unsignedbcd_1_p3), .dp(1'b0));
  // unsignedBCD unsignedbcd_1: pin names not known; wires that end beside it: unsignedbcd_1_p1, {in_1, in_2, in_3, in_4}, unsignedbcd_1_p3
  mul_by_n mul_by_n_1 (.in({in_1, in_2, in_3, in_4}), .out(mul_by_n_1_out));
  // binary2bcd binary2bcd_1: pin names not known; wires that end beside it: mul_by_n_1_out, binary2bcd_1_p2, binary2bcd_1_p3, binary2bcd_1_p4
  Seven_Seg_Hex seven_seg_hex_3 (.d(binary2bcd_1_p4), .dp(1'b0));
  Seven_Seg_Hex seven_seg_hex_4 (.d(binary2bcd_1_p3), .dp(1'b0));
  Seven_Seg_Hex seven_seg_hex_5 (.d(binary2bcd_1_p2), .dp(1'b0));

  // Notes on the sheet:
  //   x 5 =
endmodule
