// Digital circuit oct2seven.dig as structural Verilog
module oct2seven (
  input  d2,
  input  d1,
  input  d0,
  output a,
  output b,
  output c,
  output d,
  output e,
  output f,
  output g
);

  wire and_1_out, and_2_out, and_3_out, and_4_out, and_5_out, and_6_out, and_7_out, and_8_out, and_9_out,
       and_10_out, and_11_out, and_12_out, and_13_out, and_14_out, and_15_out, and_16_out, and_17_out,
       not_1_out, not_2_out, not_3_out, not_4_out, not_5_out, not_6_out, not_7_out, not_8_out, not_9_out,
       not_10_out, not_11_out, not_12_out, not_13_out, not_14_out, not_16_out, not_17_out, not_18_out,
       not_19_out, not_20_out, or_1_out, or_2_out, or_3_out, or_4_out, or_5_out, or_7_out;

  not not_1 (not_1_out, d2);
  not not_2 (not_2_out, d0);
  and and_1 (and_1_out, not_1_out, d0);
  and and_2 (and_2_out, d2, not_2_out);
  and and_3 (and_3_out, d2, not_3_out);
  not not_3 (not_3_out, d1);
  not not_4 (not_4_out, d2);
  and and_4 (and_4_out, not_4_out, d1);
  not not_5 (not_5_out, d2);
  not not_6 (not_6_out, d0);
  not not_7 (not_7_out, d1);
  not not_8 (not_8_out, d0);
  not not_9 (not_9_out, d2);
  not not_10 (not_10_out, d1);
  and and_5 (and_5_out, not_5_out, d1, not_6_out);
  and and_6 (and_6_out, d2, not_7_out, not_8_out);
  and and_7 (and_7_out, not_9_out, not_10_out, d0);
  and and_8 (and_8_out, d2, d1, d0);
  not not_11 (not_11_out, d2);
  and and_9 (and_9_out, d1, d0);
  not not_12 (not_12_out, d1);
  not not_13 (not_13_out, d2);
  or or_1 (or_1_out, and_1_out, and_2_out);
  not not_14 (not_14_out, d1);
  or or_2 (or_2_out, and_3_out, and_4_out);
  not not_15 (c, and_5_out);
  and and_10 (and_10_out, d2, not_12_out);
  and and_11 (and_11_out, not_13_out, d1);
  not not_16 (not_16_out, d1);
  not not_17 (not_17_out, d2);
  not not_18 (not_18_out, d0);
  not not_19 (not_19_out, d1);
  and and_12 (and_12_out, or_1_out, not_14_out);
  and and_13 (and_13_out, or_2_out, d0);
  or or_3 (or_3_out, and_6_out, and_7_out, and_8_out);
  not not_20 (not_20_out, d0);
  or or_4 (or_4_out, and_10_out, and_11_out);
  and and_14 (and_14_out, not_18_out, not_19_out);
  and and_15 (and_15_out, d0, d1, d2);
  or or_5 (or_5_out, and_9_out, not_20_out);
  and and_16 (and_16_out, or_4_out, d0);
  and and_17 (and_17_out, not_16_out, not_17_out);
  not not_21 (a, and_12_out);
  not not_22 (b, and_13_out);
  not not_23 (d, or_3_out);
  and and_18 (e, not_11_out, or_5_out);
  or or_6 (f, and_16_out, and_17_out);
  or or_7 (or_7_out, and_14_out, and_15_out);
  not not_24 (g, or_7_out);
endmodule
