// Digital circuit tally.dig as structural Verilog
module tally (
  input  clk,
  input  reset,
  input  button,
  output [3:0] t10,
  output [3:0] t1
);

  wire and_1_out, and_2_out, and_3_out, and_4_out, and_5_out, cntdecu_2_p5, d_ff_1_q, not_1_out, not_2_out,
       not_3_out, or_1_out;

  not not_1 (not_1_out, reset);
  not not_2 (not_2_out, button);
  D_FF d_ff_1 (.D(not_2_out), .C(clk), .Q(d_ff_1_q));  // open: nQ
  not not_3 (not_3_out, d_ff_1_q);
  and and_1 (and_1_out, not_3_out, not_2_out);
  and and_2 (and_2_out, t10[1], and_5_out);
  and and_3 (and_3_out, and_1_out, cntdecu_2_p5);
  and and_4 (and_4_out, and_2_out, and_1_out);
  or or_1 (or_1_out, and_4_out, not_1_out);
  // cntDECu cntdecu_1: pin names not known; wires that end beside it: clk, or_1_out, and_3_out, t10
  // cntDECu cntdecu_2: pin names not known; wires that end beside it: clk, or_1_out, and_1_out, t1, cntdecu_2_p5
  and and_5 (and_5_out, t1[0], t1[1]);
endmodule
